# Fritzing sketch Project (saved by Fritzing 0.9.3b)
breadboards: 2

parts:
  U1 = NodeMCU V3.0
  Part1 = Soil Moisture Sensor
  YL-83_-_Control_Board1 = YL-83 Rain Sensor - Control Board
  KY-1 = Keyes Relay [package=THT]
  VCC1 = Battery block 9V
  PSU1 = Adjustable Breadboard Power Supply
  M1 = DC Motor

nets:
  N1: U1.D0, KY-1.signal
  3V3: U1.3V3, YL-83_-_Control_Board1.VCC, KY-1.power
  N2: U1.GND#6, U1.GND#13, U1.GND#16, U1.GND#33, YL-83_-_Control_Board1.GND, KY-1.ground
  N3: U1.A0, YL-83_-_Control_Board1.AO
  N4: Part1.GND, YL-83_-_Control_Board1.NEG
  N5: Part1.VCC, YL-83_-_Control_Board1.POS
  N6: KY-1.NC, M1.pin_1
  N7: KY-1.C, PSU1.Vout+
  N8: VCC1.-, PSU1.Vin-
  N9: VCC1.+, PSU1.Vin+
  N10: PSU1.Vout-, M1.pin_2

custom parts:
  NodeMCU V3.0: ESP8266 based NodeMCU
  YL-83 Rain Sensor - Control Board: The YL-83 is a rain sensor that has more resistance when dry and less resistance when wet. The module runs at 5V.
  Keyes Relay: The Keyes 5V relay module is suitable for SCM development, home appliance control. It uses a 5V~12V TIL control signal which can control DC / AC signal.
